// Logisim project lfsr.circ as structural Verilog: 3 circuits, main circuit main
module main (
  input  C,
  input  in_2,
  output out_3,
  output out_4,
  output out_5,
  output out_6,
  output out_7,
  output out_8,
  output out_9,
  output out_10,
  output out_11,
  output out_12,
  output out_13,
  output out_14,
  output out_15,
  output out_16,
  output out_17,
  output out_18
);

  wire por_1_out, xor_1_out, xor_2_out;

  xor xor_1 (xor_1_out, out_10, out_18);
  ExactlyOne xor_2 (.out(xor_2_out), .in0(xor_1_out), .in1(por_1_out), .in2(out_3));
  POR por_1 (.out(por_1_out));
  D_Trigger_Front d_trigger_front_1 (.D(xor_2_out), .C(C), .Q(out_3));  // open: NQ
  D_Trigger_Front d_trigger_front_2 (.D(out_10), .C(C), .Q(out_11));  // open: NQ
  D_Trigger_Front d_trigger_front_3 (.D(out_3), .C(C), .Q(out_4));  // open: NQ
  D_Trigger_Front d_trigger_front_4 (.D(out_11), .C(C), .Q(out_12));  // open: NQ
  D_Trigger_Front d_trigger_front_5 (.D(out_4), .C(C), .Q(out_5));  // open: NQ
  D_Trigger_Front d_trigger_front_6 (.D(out_12), .C(C), .Q(out_13));  // open: NQ
  D_Trigger_Front d_trigger_front_7 (.D(out_5), .C(C), .Q(out_6));  // open: NQ
  D_Trigger_Front d_trigger_front_8 (.D(out_13), .C(C), .Q(out_14));  // open: NQ
  D_Trigger_Front d_trigger_front_9 (.D(out_6), .C(C), .Q(out_7));  // open: NQ
  D_Trigger_Front d_trigger_front_10 (.D(out_14), .C(C), .Q(out_15));  // open: NQ
  D_Trigger_Front d_trigger_front_11 (.D(out_7), .C(C), .Q(out_8));  // open: NQ
  D_Trigger_Front d_trigger_front_12 (.D(out_15), .C(C), .Q(out_16));  // open: NQ
  D_Trigger_Front d_trigger_front_13 (.D(out_8), .C(C), .Q(out_9));  // open: NQ
  D_Trigger_Front d_trigger_front_14 (.D(out_16), .C(C), .Q(out_17));  // open: NQ
  D_Trigger_Front d_trigger_front_15 (.D(out_9), .C(C), .Q(out_10));  // open: NQ
  D_Trigger_Front d_trigger_front_16 (.D(out_17), .C(C), .Q(out_18));  // open: NQ
endmodule

module D_Trigger (
  input  D,
  input  C,
  output Q,
  output NQ
);

  wire nand_1_out, nand_2_out, nand_4_out, por_1_out;

  nand nand_1 (nand_1_out, D, C);
  nand nand_2 (nand_2_out, nand_1_out, C);
  nand nand_3 (Q, nand_1_out, NQ);
  nand nand_4 (nand_4_out, Q, nand_2_out);
  POR por_1 (.out(por_1_out));
  or or_1 (NQ, nand_4_out, por_1_out);
endmodule

module D_Trigger_Front (
  input  D,
  input  C,
  output Q,
  output NQ
);

  wire d_trigger_1_q, not_1_out;

  not not_1 (not_1_out, C);
  D_Trigger d_trigger_1 (.D(D), .C(C), .Q(d_trigger_1_q));  // open: NQ
  D_Trigger d_trigger_2 (.D(d_trigger_1_q), .C(not_1_out), .Q(Q), .NQ(NQ));
endmodule
